// Digital circuit CORE.dig as structural Verilog
module CORE (
  input  clk,
  input  RST,
  input  CLR,
  input  in_4,
  input  [11:0] MIPCBI,
  input  [15:0] PCBI,
  input  MIPCBE,
  input  PCBE
);

  wire ALUD_CO, ALUDH_OE, ALUDL_OE, ALUS_OE, and_3_out, and_4_out, and_5_out, ASSERT_p5, BR_Q, button_1_out,
       CLK_t, CLKR, comparator_1_eq, comparator_1_gt, comparator_1_lt, comparator_2_eq, comparator_3_eq,
       DC_JUMP, DUMP_p5, EXT_p5, IMMED_OE, IRQ_OE, not_1_out, or_1_out, RAM_OE, RAM_WE, RF_HWE, RF_LWE,
       RF_SFR, RFSRCR_WE, ROM_OE, SFR_OE, SR_WE, WR_WE, XRAM_OE;
  wire [2:0] BR_SRC, BUS_SRC, JUMP_TYPE;
  wire [3:0] ALUSD_FUNC, multiplexer_2_out, RF_SRC;
  wire [5:4] multiplexer_2_out_2;
  wire [6:0] and_2_out;
  wire [7:0] DBUS, IMMED, RADDR, RF_Q, WR_q;
  wire [7:4] RFSRCR_q;
  wire [11:0] ADDRESS, MIPC;
  wire [15:0] pce_1_q;
  wire [47:44] DECODER_2_d;

  DCOUTER #(.generic("Bits := 12;")) dcouter_1 (
    .CLK(CLK_t), .CLR(CLR), .CNT(1'b1), .LE(DC_JUMP), .D(ADDRESS), .Q(MIPC));
  Comparator #(.Bits(8)) comparator_1 (
    .a(RF_Q), .b(IMMED), .gt(comparator_1_gt), .eq(comparator_1_eq), .lt(comparator_1_lt));
  Decoder #(.Selector_Bits(3)) decoder_1 (
    .sel(BUS_SRC), .out_0(ALUS_OE), .out_1(ALUDL_OE), .out_2(ALUDH_OE), .out_3(IMMED_OE), .out_4(RAM_OE),
    .out_5(XRAM_OE), .out_6(ROM_OE), .out_7(IRQ_OE));
  Multiplexer #(.Selector_Bits(3)) multiplexer_1 (
    .sel(JUMP_TYPE), .in_0(1'b0), .in_1(1'b1), .in_2(comparator_1_gt), .in_3(comparator_1_eq),
    .in_4(comparator_1_lt), .in_5(BR_Q), .in_6(RST), .in_7(1'b0), .out(DC_JUMP));
  PCE pce_1 (.CLK(CLK_t), .D(DBUS), .RS(RF_SRC), .LWE(RF_LWE), .HWE(RF_HWE), .Q(pce_1_q));
  ROM #(.AddrBits(12), .Bits(48)) DECODER_2 (
    .A(MIPC), .sel(1'b1),
    .D({DECODER_2_d, IMMED, ADDRESS, JUMP_TYPE, ALUSD_FUNC, RAM_WE, RFSRCR_WE, BR_SRC, SR_WE, WR_WE, BUS_SRC, RF_SFR, RF_HWE, RF_LWE, RF_SRC}));
  Register #(.Bits(8)) RFSRCR (.D(DBUS), .C(CLK_t), .en(RFSRCR_WE), .Q({RFSRCR_q, and_2_out[3:0]}));
  and and_1 (and_2_out[5], RFSRCR_q[4], RAM_WE);
  and and_2 (and_2_out[6], RFSRCR_q[4], RAM_OE);
  Comparator #(.Bits(12)) comparator_2 (.a(MIPCBI), .b(MIPC), .eq(comparator_2_eq));  // open: gt, lt
  Comparator #(.Bits(16)) comparator_3 (.a(PCBI), .b(pce_1_q), .eq(comparator_3_eq));  // open: gt, lt
  and and_3 (and_3_out, comparator_2_eq, MIPCBE);
  and and_4 (and_4_out, comparator_3_eq, PCBE);
  Multiplexer #(.Bits(7)) multiplexer_2 (
    .sel(RF_SFR), .in_0({1'b0, RF_HWE, RF_LWE, RF_SRC}),
    .in_1({and_2_out[6:5], and_2_out[5], and_2_out[3:0]}),
    .out({SFR_OE, multiplexer_2_out_2, multiplexer_2_out}));
  // Probe on MIPC
  // Probe on RF_SRC
  // Probe on RF_LWE
  // Probe on RF_HWE
  // Probe on RF_SFR
  // Probe on BUS_SRC
  // Probe on WR_WE
  // Probe on SR_WE
  // Probe on BR_SRC
  // Probe on RFSRCR_WE
  // Probe on RAM_WE
  // Probe on ALUSD_FUNC
  // Probe on JUMP_TYPE
  // Probe on ADDRESS
  // Probe on IMMED
  // ASSERT ASSERT: pin names not known; wires that end beside it: CLK_t, DBUS, RADDR, RAM_WE, ASSERT_p5, CLK_t
  Button button_1 (.out(button_1_out));
  // reg_file RF: pin names not known; wires that end beside it: CLK_t, multiplexer_2_out, DBUS, multiplexer_2_out_2[4], multiplexer_2_out_2[5], RF_Q
  BR BR (.CLK(CLK_t), .nCLR(CLR), .S(BR_SRC), .I4(ALUD_CO), .I5(ALUD_CO), .I7(RF_Q[0]), .I6(RF_Q[7]), .Q(BR_Q));
  or or_1 (or_1_out, ASSERT_p5, and_3_out, and_4_out);
  // SwitchDT switchdt_1: pin names not known; wires that end beside it: clk, button_1_out, CLKR
  // Probe on RF_Q
  STALL STALL (.C(CLKR), .AC(or_1_out), .S(in_4), .OAC(CLK_t));  // open: G, nCLR, O
  reg__sync_clear #(.generic("Bits := 8;")) WR (.D(DBUS), .CLK(CLK_t), .CLR(CLR), .LE(WR_WE), .Q(WR_q));
  reg__sync_clear #(.generic("Bits := 8;")) SR (.D(DBUS), .CLK(CLK_t), .CLR(CLR), .LE(SR_WE), .Q(RADDR));
  not not_1 (not_1_out, CLK_t);
  PullDown #(.Bits(8)) pulldown_1 (.out(DBUS));
  assign DBUS = SFR_OE ? RF_Q : 8'bz;  // Driver driver_1
  // Probe on WR_q
  // Probe on RADDR
  and and_5 (and_5_out, RAM_WE, CLK_t, not_1_out);
  // Probe on DBUS
  ALU ALU (
    .A(RF_Q), .B(WR_q), .S(ALUSD_FUNC), .CI(BR_Q), .SOE(ALUS_OE), .DOE(ALUDL_OE), .FOE(ALUDH_OE), .O(DBUS),
    .ALUDF(ALUD_CO));
  // Probe on {RADDR, WR_q}
  ROM #(.AddrBits(16), .Bits(8)) ROM (.A({RADDR, WR_q}), .sel(ROM_OE), .D(DBUS));
  RAMSinglePortSel #(.AddrBits(7), .isProgramMemory("true"), .Bits(8)) RAM (
    .A(RADDR[6:0]), .CS(~RADDR[7]), .WE(and_5_out), .OE(RAM_OE), .D(DBUS));
  // EXTCTL EXT: pin names not known; wires that end beside it: RAM_WE, RADDR, DBUS, CLK_t, EXT_p5
  // DUMP DUMP: pin names not known; wires that end beside it: RAM_WE, RADDR, DBUS, CLK_t, DUMP_p5
  // Probe on EXT_p5
  assign DBUS = IMMED_OE ? IMMED : 8'bz;  // Driver driver_2
  // Probe on DUMP_p5

  // Other names for the same wires on the sheet: GO = in_4

  // Notes on the sheet:
  //   clk: Hz: 2147483647
  //   contents of DECODER_2 (hex, n*v repeats v):
  //   151c80488,80889,33a,85106,1c3135,1e54b8,1e08b9,8008a80000a,c004480000a,e002580000a,
  //   f001680000a,f801080040a,a00bc,80485,1a088c,236,f401380000a,f601280000a,f501380000a,
  //   f201580000a,f301580000a,f101680000a,e801e80000a,ec01b80000a,ee01a80000a,ef01a80000a,
  //   ed01b80000a,ea01d80000a,eb01d80000a,e901e80000a,e402280000a,e602180000a,e702180000a,
  //   e502280000a,e202480000a,e302480000a,e102580000a,d003580000a,d802e80000a,dc02b80000a,
  //   de02a80000a,df02a80000a,dd02b80000a,da02d80000a,db02d80000a,d902e80000a,d403280000a,
  //   d603180000a,d703180000a,d503280000a,d203480000a,d303480000a,d103580000a,c803d80000a,
  //   cc03a80000a,ce03980000a,cf03980000a,cd03a80000a,ca03c80000a,cb03c80000a,c903d80000a,
  //   c404180000a,c604080000a,c704080000a,c504180000a,c204380000a,c304380000a,c104480000a,
  //   a006780000a,b005580000a,b804e80000a,bc04b80000a,be04a80000a,bf04a80000a,bd04b80000a,
  //   ba04d80000a,bb04d80000a,b904e80000a,b405280000a,b605180000a,b705180000a,b505280000a,
  //   b205480000a,b305480000a,b105580000a,a805d80000a,ac05a80000a,ae05980000a,af05980000a,
  //   ad05a80000a,aa05c80000a,ab05c80000a,a905d80000a,a406180000a,a606080000a,a706080000a,
  //   a506180000a,a206680000a,a306680000a,3580,450b1,1392400b2,a106780000a,9006f80000a,
  //   9806980000a,9406c80000a,9606b80000a,9506c80000a,9206e80000a,9306e80000a,9106f80000a,
  //   8807780000a,8c07480000a,8e07380000a,8f07380000a,8d07480000a,8a07680000a,8b07680000a,
  //   8907780000a,8408780000a,8607a80000a,8707a80000a,8508780000a,b3c,6800c,640,a30bd,1e54b8,
  //   1e08b9,b3c,8048d,6800c,b30c0,1e54b8,1393e08b9,8208980000a,8308980000a,8108a80000a,
  //   400d380000a,600b480000a,700a580000a,7809580000a,7c09280000a,7e09180000a,7f09180000a,
  //   7d09280000a,7a09480000a,7b09480000a,7909580000a,740a280000a,7609880000a,7709880000a,
  //   750a280000a,333c,1e54b8,1e08b9,700,6800c,8088c,b30c0,1e54b8,1393e08b9,720a480000a,
  //   730a480000a,710a580000a,680ad80000a,6c0aa80000a,6e0a980000a,6f0a980000a,6d0aa80000a,
  //   6a0ac80000a,6b0ac80000a,690ad80000a,640b180000a,660b080000a,670b080000a,650b180000a,
  //   620b380000a,630b380000a,610b480000a,500c480000a,580bd80000a,5c0ba80000a,5e0b980000a,
  //   5f0b980000a,5d0ba80000a,5a0bc80000a,5b0bc80000a,590bd80000a,540c180000a,560c080000a,
  //   570c080000a,550c180000a,520c380000a,530c380000a,510c480000a,480cc80000a,4c0c980000a,
  //   4e0c880000a,4f0c880000a,4d0c980000a,4a0cb80000a,4b0cb80000a,490cc80000a,440d080000a,
  //   460cf80000a,470cf80000a,450d080000a,420d280000a,430d280000a,410d380000a,2010180000a,
  //   300e780000a,380dd80000a,3c0da80000a,3e0d980000a,3f0d980000a,3d0da80000a,3a0dc80000a,
  //   3b0dc80000a,390dd80000a,340e180000a,360e080000a,370e080000a,350e180000a,320e680000a,
  //   330e680000a,6005,e6036,139380035,310e780000a,280ef80000a,2c0ec80000a,2e0eb80000a,
  //   2f0eb80000a,2d0ec80000a,2a0ee80000a,2b0ee80000a,290ef80000a,240fd80000a,260f280000a,
  //   270f280000a,250f380000a,80486,a00bc,273d,4013c,40c,1c0135,8048d,430b6,1e54b8,1393e08b9,
  //   2210080000a,2310080000a,1392a0036,2110180000a,1011e80000a,1810780000a,80485,1a088a,
  //   23c,13933000c,1411880000a,1610e80000a,80485,18088a,a00,23c,13933300c,1511780000a,
  //   b3c,6800c,640,a00bc,12040c,b30c0,1e54b8,1393e08b9,139320036,1211d80000a,1311d80000a,
  //   6005,c7036,139380035,1111e80000a,812380000a,80485,1a088a,23c,13931000c,413480000a,
  //   612a80000a,80485,18088a,a00,23c,13931300c,513380000a,b3c,6800c,640,a00bc,10040c,b30c0,
  //   1e54b8,1393e08b9,139300036,213780000a,313780000a,139280036,113980000a,139200000,80000880483,
  //   3bc,e04bc,100080000c,80484,1600bc,8048b,a00bd,a00be,80484,16348d,6508c,a00000,10048c,
  //   e00be,40000e,c00bb,100830,90088,100830,90089,2043c,1b9,2a00b8,1b6,1b7,1b0,1b5,1b1,
  //   1b2,1b3,1b4,1b8,1b9,1ba,151c001bb,200000
  //   contents of ROM (hex, n*v repeats v):
  //   75,81,0,75,82,0,75,83,0,75,d0,0,75,e0,0,75,f0,0,24,0,85,e0,fd,75,fe,0,75,ff,2,24,
  //   1,85,e0,fd,75,fe,1,75,ff,2,24,2,85,e0,fd,75,fe,3,75,ff,2,24,3,85,e0,fd,75,fe,6,75,
  //   ff,2,24,4,85,e0,fd,75,fe,a,75,ff,2,24,5,85,e0,fd,75,fe,f,75,ff,2,24,6,85,e0,fd,75,
  //   fe,15,75,ff,2,24,7,85,e0,fd,75,fe,1c,75,ff,2,24,8,85,e0,fd,75,fe,24,75,ff,2,24,9,
  //   85,e0,fd,75,fe,2d,75,ff,2,24,a,85,e0,fd,75,fe,37,75,ff,2,24,b,85,e0,fd,75,fe,42,75,
  //   ff,2,24,c,85,e0,fd,75,fe,4e,75,ff,2,24,d,85,e0,fd,75,fe,5b,75,ff,2,24,e,85,e0,fd,
  //   75,fe,69,75,ff,2,24,f,85,e0,fd,75,fe,78,75,ff,2,24,10,85,e0,fd,75,fe,88,75,ff,2,24,
  //   11,85,e0,fd,75,fe,99,75,ff,2,24,12,85,e0,fd,75,fe,ab,75,ff,2,24,13,85,e0,fd,75,fe,
  //   be,75,ff,2,24,14,85,e0,fd,75,fe,d2,75,ff,2,24,15,85,e0,fd,75,fe,e7,75,ff,2,24,16,
  //   85,e0,fd,75,fe,fd,75,ff,2,24,17,85,e0,fd,75,fe,14,75,ff,2,24,18,85,e0,fd,75,fe,2c,
  //   75,ff,2,24,19,85,e0,fd,75,fe,45,75,ff,2,24,1a,85,e0,fd,75,fe,5f,75,ff,2,24,1b,85,
  //   e0,fd,75,fe,7a,75,ff,2,24,1c,85,e0,fd,75,fe,96,75,ff,2,24,1d,85,e0,fd,75,fe,b3,75,
  //   ff,2,24,1e,85,e0,fd,75,fe,d1,75,ff,2,24,1f,85,e0,fd,75,fe,f0,75,ff,2,24,20,85,e0,
  //   fd,75,fe,10,75,ff,2,24,21,85,e0,fd,75,fe,31,75,ff,2,24,22,85,e0,fd,75,fe,53,75,ff,
  //   2,24,23,85,e0,fd,75,fe,76,75,ff,2,24,24,85,e0,fd,75,fe,9a,75,ff,2,24,25,85,e0,fd,
  //   75,fe,bf,75,ff,2,24,26,85,e0,fd,75,fe,e5,75,ff,2,24,27,85,e0,fd,75,fe,c,75,ff,2,24,
  //   28,85,e0,fd,75,fe,34,75,ff,2,24,29,85,e0,fd,75,fe,5d,75,ff,2,24,2a,85,e0,fd,75,fe,
  //   87,75,ff,2,24,2b,85,e0,fd,75,fe,b2,75,ff,2,24,2c,85,e0,fd,75,fe,de,75,ff,2,24,2d,
  //   85,e0,fd,75,fe,b,75,ff,2,24,2e,85,e0,fd,75,fe,39,75,ff,2,24,2f,85,e0,fd,75,fe,68,
  //   75,ff,2,24,30,85,e0,fd,75,fe,98,75,ff,2,24,31,85,e0,fd,75,fe,c9,75,ff,2,24,32,85,
  //   e0,fd,75,fe,fb,75,ff,2,24,33,85,e0,fd,75,fe,2e,75,ff,2,24,34,85,e0,fd,75,fe,62,75,
  //   ff,2,24,35,85,e0,fd,75,fe,97,75,ff,2,24,36,85,e0,fd,75,fe,cd,75,ff,2,24,37,85,e0,
  //   fd,75,fe,4,75,ff,2,24,38,85,e0,fd,75,fe,3c,75,ff,2,24,39,85,e0,fd,75,fe,75,75,ff,
  //   2,24,3a,85,e0,fd,75,fe,af,75,ff,2,24,3b,85,e0,fd,75,fe,ea,75,ff,2,24,3c,85,e0,fd,
  //   75,fe,26,75,ff,2,24,3d,85,e0,fd,75,fe,63,75,ff,2,24,3e,85,e0,fd,75,fe,a1,75,ff,2,
  //   24,3f,85,e0,fd,75,fe,e0,75,ff,2,24,40,85,e0,fd,75,fe,20,75,ff,2,24,41,85,e0,fd,75,
  //   fe,61,75,ff,2,24,42,85,e0,fd,75,fe,a3,75,ff,2,24,43,85,e0,fd,75,fe,e6,75,ff,2,24,
  //   44,85,e0,fd,75,fe,2a,75,ff,2,24,45,85,e0,fd,75,fe,6f,75,ff,2,24,46,85,e0,fd,75,fe,
  //   b5,75,ff,2,24,47,85,e0,fd,75,fe,fc,75,ff,2,24,48,85,e0,fd,75,fe,44,75,ff,2,24,49,
  //   85,e0,fd,75,fe,8d,75,ff,2,24,4a,85,e0,fd,75,fe,d7,75,ff,2,24,4b,85,e0,fd,75,fe,22,
  //   75,ff,2,24,4c,85,e0,fd,75,fe,6e,75,ff,2,24,4d,85,e0,fd,75,fe,bb,75,ff,2,24,4e,85,
  //   e0,fd,75,fe,9,75,ff,2,24,4f,85,e0,fd,75,fe,58,75,ff,2,24,50,85,e0,fd,75,fe,a8,75,
  //   ff,2,24,51,85,e0,fd,75,fe,f9,75,ff,2,24,52,85,e0,fd,75,fe,4b,75,ff,2,24,53,85,e0,
  //   fd,75,fe,9e,75,ff,2,24,54,85,e0,fd,75,fe,f2,75,ff,2,24,55,85,e0,fd,75,fe,47,75,ff,
  //   2,24,56,85,e0,fd,75,fe,9d,75,ff,2,24,57,85,e0,fd,75,fe,f4,75,ff,2,24,58,85,e0,fd,
  //   75,fe,4c,75,ff,2,24,59,85,e0,fd,75,fe,a5,75,ff,2,24,5a,85,e0,fd,75,fe,ff,75,ff,2,
  //   24,5b,85,e0,fd,75,fe,5a,75,ff,2,24,5c,85,e0,fd,75,fe,b6,75,ff,2,24,5d,85,e0,fd,75,
  //   fe,13,75,ff,2,24,5e,85,e0,fd,75,fe,71,75,ff,2,24,5f,85,e0,fd,75,fe,d0,75,ff,2,24,
  //   60,85,e0,fd,75,fe,30,75,ff,2,24,61,85,e0,fd,75,fe,91,75,ff,2,24,62,85,e0,fd,75,fe,
  //   f3,75,ff,2,24,63,85,e0,fd,75,fe,56,75,ff,2,24,64,85,e0,fd,75,fe,ba,75,ff,2,24,65,
  //   85,e0,fd,75,fe,1f,75,ff,2,24,66,85,e0,fd,75,fe,85,75,ff,2,24,67,85,e0,fd,75,fe,ec,
  //   75,ff,2,24,68,85,e0,fd,75,fe,54,75,ff,2,24,69,85,e0,fd,75,fe,bd,75,ff,2,24,6a,85,
  //   e0,fd,75,fe,27,75,ff,2,24,6b,85,e0,fd,75,fe,92,75,ff,2,24,6c,85,e0,fd,75,fe,fe,75,
  //   ff,2,24,6d,85,e0,fd,75,fe,6b,75,ff,2,24,6e,85,e0,fd,75,fe,d9,75,ff,2,24,6f,85,e0,
  //   fd,75,fe,48,75,ff,2,24,70,85,e0,fd,75,fe,b8,75,ff,2,24,71,85,e0,fd,75,fe,29,75,ff,
  //   2,24,72,85,e0,fd,75,fe,9b,75,ff,2,24,73,85,e0,fd,75,fe,e,75,ff,2,24,74,85,e0,fd,75,
  //   fe,82,75,ff,2,24,75,85,e0,fd,75,fe,f7,75,ff,2,24,76,85,e0,fd,75,fe,6d,75,ff,2,24,
  //   77,85,e0,fd,75,fe,e4,75,ff,2,24,78,85,e0,fd,75,fe,5c,75,ff,2,24,79,85,e0,fd,75,fe,
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endmodule
